// Digital circuit Delay-Line.dig as structural Verilog
module Delay_Line (
  input  clk
);

  wire _7447_1_pin1, _7447_1_pin2, _7447_1_pin6, _7447_1_pin7, _7447_1_pin9, _7447_1_pin10, _7447_1_pin11,
       _7447_1_pin12, _7447_1_pin13, _7447_1_pin14, _7447_1_pin15, _7447_2_pin1, _7447_2_pin2, _7447_2_pin6,
       _7447_2_pin7, _7447_2_pin9, _7447_2_pin10, _7447_2_pin11, _7447_2_pin12, _7447_2_pin13, _7447_2_pin14,
       _7447_2_pin15, _7447_3_pin1, _7447_3_pin2, _7447_3_pin7, _7447_3_pin9, _7447_3_pin10, _7447_3_pin11,
       _7447_3_pin12, _7447_3_pin13, _7447_3_pin14, _7447_3_pin15, _7447_4_pin9, _7447_4_pin10,
       _7447_4_pin11, _7447_4_pin12, _7447_4_pin13, _7447_4_pin14, _7447_4_pin15, _7447_5_pin9,
       _7447_5_pin10, _7447_5_pin11, _7447_5_pin12, _7447_5_pin13, _7447_5_pin14, _7447_5_pin15,
       _74157_1_pin4, _74160_1_pin1, _74160_1_pin12, _74160_1_pin13, _74160_1_pin14, _74160_2_pin1,
       _74160_2_pin10, _74160_2_pin11, _74163_1_pin2, _74163_1_pin12, _74163_1_pin13, _74163_1_pin14,
       _74164_1_pin1, _74164_2_pin1, _74164_2_pin3, _74164_2_pin4, _74164_2_pin5, _74164_2_pin6,
       _74164_2_pin10, _74164_2_pin11, _74164_2_pin12, _74164_3_pin1, _74164_3_pin3, _74164_3_pin4,
       _74164_3_pin5, _74164_3_pin6, _74164_3_pin10, _74164_3_pin11, _74164_3_pin12, _74164_4_pin3,
       _74164_4_pin4, _74164_4_pin5, _74164_4_pin6, _74164_4_pin10, _74164_4_pin11, _74164_4_pin12,
       _74164_4_pin13, _74164_5_pin1, _74164_5_pin3, _74164_5_pin4, _74164_5_pin5, _74164_5_pin6,
       _74164_5_pin10, _74164_5_pin11, _74164_5_pin12, _74164_6_pin3, _74164_6_pin4, _74164_6_pin5,
       _74164_6_pin6, _74164_6_pin10, _74164_6_pin11, _74164_6_pin12, _74164_6_pin13, _74164_7_pin1,
       _74164_7_pin3, _74164_7_pin4, _74164_7_pin5, _74164_7_pin6, _74164_7_pin10, _74164_7_pin11,
       _74164_7_pin12, _74164_8_pin3, _74164_8_pin4, _74164_8_pin5, _74164_8_pin6, _74164_8_pin10,
       _74164_8_pin11, _74164_8_pin12, _74164_8_pin13, _74164_9_pin3, _74164_9_pin4, _74164_9_pin5,
       _74164_9_pin6, _74164_9_pin10, _74164_9_pin11, _74164_9_pin12, _74165_1_pin9, _74165_1_pin15,
       _74374_1_pin3, _74374_1_pin4, _74374_1_pin7, _74374_1_pin8, _74374_1_pin11, _74374_1_pin13,
       _74374_1_pin14, _74374_1_pin17, _74374_1_pin18, button_1_out, dipswitch_1_out, dipswitch_2_out,
       dipswitch_3_out, dipswitch_4_out, dipswitch_5_out, dipswitch_6_out, dipswitch_10_out,
       dipswitch_11_out, nand_1_out, nand_2_out, switch_1_a, switch_1_b;

  LED led_1 (.in(_7447_1_pin6));
  LED led_2 (.in(_7447_1_pin2));
  LED led_3 (.in(_7447_1_pin1));
  LED led_4 (.in(_7447_1_pin7));
  LED led_5 (.in(_7447_2_pin6));
  LED led_6 (.in(_7447_2_pin2));
  LED led_7 (.in(_7447_2_pin1));
  LED led_8 (.in(_7447_2_pin7));
  _7447 _7447_1 (
    .pin1(_7447_1_pin1), .pin2(_7447_1_pin2), .pin3(1'b1), .pin4(1'b1), .pin5(1'b1), .pin6(_7447_1_pin6),
    .pin7(_7447_1_pin7), .pin8(1'b0), .pin9(_7447_1_pin9), .pin10(_7447_1_pin10), .pin11(_7447_1_pin11),
    .pin12(_7447_1_pin12), .pin13(_7447_1_pin13), .pin14(_7447_1_pin14), .pin15(_7447_1_pin15), .pin16(1'b1));
  Seven_Seg #(.commonCathode("true"), .commonConnectionType("anode")) seven_seg_1 (
    .a(_7447_1_pin13), .b(_7447_1_pin12), .c(_7447_1_pin11), .d(_7447_1_pin10), .e(_7447_1_pin9),
    .f(_7447_1_pin15), .g(_7447_1_pin14), .dp(1'b1), .common(1'b1));
  _7447 _7447_2 (
    .pin1(_7447_2_pin1), .pin2(_7447_2_pin2), .pin3(1'b1), .pin4(1'b1), .pin5(1'b1), .pin6(_7447_2_pin6),
    .pin7(_7447_2_pin7), .pin8(1'b0), .pin9(_7447_2_pin9), .pin10(_7447_2_pin10), .pin11(_7447_2_pin11),
    .pin12(_7447_2_pin12), .pin13(_7447_2_pin13), .pin14(_7447_2_pin14), .pin15(_7447_2_pin15), .pin16(1'b1));
  _74374 _74374_1 (
    .pin1(1'b0), .pin2(_7447_1_pin6), .pin3(_74374_1_pin3), .pin4(_74374_1_pin4), .pin5(_7447_1_pin2),
    .pin6(_7447_1_pin1), .pin7(_74374_1_pin7), .pin8(_74374_1_pin8), .pin9(_7447_1_pin7), .pin10(1'b0),
    .pin11(_74374_1_pin11), .pin12(_7447_2_pin6), .pin13(_74374_1_pin13), .pin14(_74374_1_pin14),
    .pin15(_7447_2_pin2), .pin16(_7447_2_pin1), .pin17(_74374_1_pin17), .pin18(_74374_1_pin18),
    .pin19(_7447_2_pin7), .pin20(1'b1));
  _74164 _74164_1 (
    .pin1(_74164_1_pin1), .pin2(_74164_1_pin1), .pin3(_74374_1_pin3), .pin4(_74374_1_pin4),
    .pin5(_74374_1_pin7), .pin6(_74374_1_pin8), .pin7(1'b0), .pin8(clk), .pin9(1'b1), .pin10(_74374_1_pin13),
    .pin11(_74374_1_pin14), .pin12(_74374_1_pin17), .pin13(_74374_1_pin18), .pin14(1'b1));
  Seven_Seg #(.commonCathode("true"), .commonConnectionType("anode")) seven_seg_2 (
    .a(_7447_2_pin13), .b(_7447_2_pin12), .c(_7447_2_pin11), .d(_7447_2_pin10), .e(_7447_2_pin9),
    .f(_7447_2_pin15), .g(_7447_2_pin14), .dp(1'b1), .common(1'b1));
  LED led_9 (.in(switch_1_b));
  _7447 _7447_3 (
    .pin1(_7447_3_pin1), .pin2(_7447_3_pin2), .pin3(1'b1), .pin4(1'b1), .pin5(1'b1), .pin6(1'b0),
    .pin7(_7447_3_pin7), .pin8(1'b0), .pin9(_7447_3_pin9), .pin10(_7447_3_pin10), .pin11(_7447_3_pin11),
    .pin12(_7447_3_pin12), .pin13(_7447_3_pin13), .pin14(_7447_3_pin14), .pin15(_7447_3_pin15), .pin16(1'b1));
  Seven_Seg #(.commonCathode("true"), .commonConnectionType("anode")) seven_seg_3 (
    .a(_7447_3_pin13), .b(_7447_3_pin12), .c(_7447_3_pin11), .d(_7447_3_pin10), .e(_7447_3_pin9),
    .f(_7447_3_pin15), .g(_7447_3_pin14), .dp(1'b1), .common(1'b1));
  and and_1 (_74374_1_pin11, switch_1_b, _74163_1_pin2);
  Switch switch_1 (.A(switch_1_a), .B(switch_1_b));
  DipSwitch dipswitch_1 (.out(dipswitch_1_out));
  DipSwitch dipswitch_2 (.out(dipswitch_2_out));
  DipSwitch dipswitch_3 (.out(dipswitch_3_out));
  DipSwitch dipswitch_4 (.out(dipswitch_4_out));
  DipSwitch dipswitch_5 (.out(dipswitch_5_out));
  DipSwitch dipswitch_6 (.out(dipswitch_6_out));
  DipSwitch dipswitch_7 (.out(_7447_3_pin2));
  DipSwitch dipswitch_8 (.out(_7447_3_pin1));
  DipSwitch dipswitch_9 (.out(_7447_3_pin7));
  DipSwitch dipswitch_10 (.out(dipswitch_10_out));
  DipSwitch dipswitch_11 (.out(dipswitch_11_out));
  _74163 _74163_1 (
    .pin1(1'b1), .pin2(_74163_1_pin2), .pin3(1'b0), .pin4(1'b0), .pin5(1'b0), .pin6(1'b0), .pin7(1'b1),
    .pin8(1'b0), .pin9(1'b1), .pin10(1'b1), .pin12(_74163_1_pin12), .pin13(_74163_1_pin13),
    .pin14(_74163_1_pin14), .pin16(1'b1));  // open: pin11, pin15
  PullUp pullup_1 (.out(switch_1_a));
  _7447 _7447_4 (
    .pin1(_74163_1_pin13), .pin2(_74163_1_pin12), .pin3(1'b1), .pin4(1'b1), .pin5(1'b1), .pin6(1'b0),
    .pin7(_74163_1_pin14), .pin8(1'b0), .pin9(_7447_4_pin9), .pin10(_7447_4_pin10), .pin11(_7447_4_pin11),
    .pin12(_7447_4_pin12), .pin13(_7447_4_pin13), .pin14(_7447_4_pin14), .pin15(_7447_4_pin15), .pin16(1'b1));
  _7485 _7485_1 (
    .pin1(1'b1), .pin2(1'b1), .pin3(1'b1), .pin4(1'b1), .pin6(switch_1_b), .pin8(1'b0), .pin9(_7447_3_pin7),
    .pin10(_74163_1_pin14), .pin11(_74163_1_pin13), .pin12(_7447_3_pin1), .pin13(_74163_1_pin12),
    .pin14(_7447_3_pin2), .pin15(1'b1), .pin16(1'b1));  // open: pin5, pin7
  _74165 _74165_1 (
    .pin1(switch_1_a), .pin2(clk), .pin3(dipswitch_5_out), .pin4(dipswitch_6_out), .pin5(dipswitch_10_out),
    .pin6(dipswitch_11_out), .pin8(1'b0), .pin9(_74165_1_pin9), .pin10(1'b0), .pin11(dipswitch_1_out),
    .pin12(dipswitch_2_out), .pin13(dipswitch_3_out), .pin14(dipswitch_4_out), .pin15(_74165_1_pin15),
    .pin16(1'b1));  // open: pin7
  Seven_Seg #(.commonCathode("true"), .commonConnectionType("anode")) seven_seg_4 (
    .a(_7447_4_pin13), .b(_7447_4_pin12), .c(_7447_4_pin11), .d(_7447_4_pin10), .e(_7447_4_pin9),
    .f(_7447_4_pin15), .g(_7447_4_pin14), .dp(1'b1), .common(1'b1));
  _74160 _74160_1 (
    .pin1(_74160_1_pin1), .pin2(clk), .pin3(1'b0), .pin4(1'b0), .pin5(1'b0), .pin6(1'b0), .pin7(1'b1),
    .pin8(1'b0), .pin9(1'b1), .pin10(1'b1), .pin11(_74163_1_pin2), .pin12(_74160_1_pin12),
    .pin13(_74160_1_pin13), .pin14(_74160_1_pin14), .pin16(1'b1));  // open: pin15
  _7447 _7447_5 (
    .pin1(_74160_1_pin13), .pin2(_74160_1_pin12), .pin3(1'b1), .pin4(1'b1), .pin5(1'b1), .pin6(1'b0),
    .pin7(_74160_1_pin14), .pin8(1'b0), .pin9(_7447_5_pin9), .pin10(_7447_5_pin10), .pin11(_7447_5_pin11),
    .pin12(_7447_5_pin12), .pin13(_7447_5_pin13), .pin14(_7447_5_pin14), .pin15(_7447_5_pin15), .pin16(1'b1));
  _74160 _74160_2 (
    .pin1(_74160_2_pin1), .pin2(clk), .pin3(1'b0), .pin4(1'b0), .pin5(1'b0), .pin6(1'b0), .pin7(1'b1),
    .pin8(1'b0), .pin9(1'b1), .pin10(_74160_2_pin10), .pin11(_74160_2_pin11), .pin16(1'b1));  // open: pin12, pin13, pin14, pin15
  Seven_Seg #(.commonCathode("true"), .commonConnectionType("anode")) seven_seg_5 (
    .a(_7447_5_pin13), .b(_7447_5_pin12), .c(_7447_5_pin11), .d(_7447_5_pin10), .e(_7447_5_pin9),
    .f(_7447_5_pin15), .g(_7447_5_pin14), .dp(1'b1), .common(1'b1));
  nand nand_1 (nand_1_out, switch_1_a, nand_2_out);
  nand nand_2 (nand_2_out, nand_1_out, _74160_2_pin1);
  nand nand_3 (_74160_2_pin1, _74160_2_pin11, _74160_2_pin11);
  LED led_10 (.in(nand_1_out));
  LED led_11 (.in(nand_2_out));
  nand nand_4 (_74165_1_pin15, _74160_2_pin10, _74160_2_pin10);
  and and_2 (_74160_2_pin10, switch_1_b, nand_1_out);
  _74157 _74157_1 (
    .pin1(_74160_2_pin10), .pin2(_74164_1_pin1), .pin3(_74165_1_pin9), .pin4(_74157_1_pin4), .pin5(1'b0),
    .pin6(1'b0), .pin8(1'b0), .pin10(1'b0), .pin11(1'b0), .pin13(1'b0), .pin14(1'b0), .pin15(1'b0),
    .pin16(1'b1));  // open: pin7, pin9, pin12
  nand nand_5 (_74160_1_pin1, _74163_1_pin2, _74163_1_pin2);
  LED led_12 (.in(_74160_2_pin10));
  Button #(.activeLow("true")) button_1 (.out(button_1_out));
  _74164 _74164_2 (
    .pin1(_74164_2_pin1), .pin2(_74164_2_pin1), .pin3(_74164_2_pin3), .pin4(_74164_2_pin4),
    .pin5(_74164_2_pin5), .pin6(_74164_2_pin6), .pin7(1'b0), .pin8(clk), .pin9(button_1_out),
    .pin10(_74164_2_pin10), .pin11(_74164_2_pin11), .pin12(_74164_2_pin12), .pin13(_74164_1_pin1),
    .pin14(1'b1));
  _74164 _74164_3 (
    .pin1(_74164_3_pin1), .pin2(_74164_3_pin1), .pin3(_74164_3_pin3), .pin4(_74164_3_pin4),
    .pin5(_74164_3_pin5), .pin6(_74164_3_pin6), .pin7(1'b0), .pin8(clk), .pin9(button_1_out),
    .pin10(_74164_3_pin10), .pin11(_74164_3_pin11), .pin12(_74164_3_pin12), .pin13(_74164_2_pin1),
    .pin14(1'b1));
  PullUp pullup_2 (.out(button_1_out));
  LED led_13 (.in(_74164_4_pin3));
  LED led_14 (.in(_74164_1_pin1));
  LED led_15 (.in(_74164_2_pin12));
  LED led_16 (.in(_74164_2_pin11));
  LED led_17 (.in(_74164_2_pin10));
  LED led_18 (.in(_74164_2_pin6));
  LED led_19 (.in(_74164_2_pin5));
  LED led_20 (.in(_74164_2_pin4));
  LED led_21 (.in(_74164_2_pin3));
  LED led_22 (.in(_74164_2_pin1));
  LED led_23 (.in(_74164_3_pin12));
  LED led_24 (.in(_74164_3_pin11));
  LED led_25 (.in(_74164_3_pin10));
  LED led_26 (.in(_74164_3_pin6));
  LED led_27 (.in(_74164_3_pin5));
  LED led_28 (.in(_74164_3_pin4));
  LED led_29 (.in(_74164_3_pin3));
  _74164 _74164_4 (
    .pin1(_74157_1_pin4), .pin2(_74157_1_pin4), .pin3(_74164_4_pin3), .pin4(_74164_4_pin4),
    .pin5(_74164_4_pin5), .pin6(_74164_4_pin6), .pin7(1'b0), .pin8(clk), .pin9(button_1_out),
    .pin10(_74164_4_pin10), .pin11(_74164_4_pin11), .pin12(_74164_4_pin12), .pin13(_74164_4_pin13),
    .pin14(1'b1));
  LED led_30 (.in(_74164_4_pin4));
  LED led_31 (.in(_74164_4_pin5));
  LED led_32 (.in(_74164_5_pin12));
  LED led_33 (.in(_74164_3_pin1));
  LED led_34 (.in(_74164_4_pin6));
  LED led_35 (.in(_74164_4_pin10));
  LED led_36 (.in(_74164_5_pin10));
  LED led_37 (.in(_74164_5_pin11));
  LED led_38 (.in(_74164_4_pin11));
  LED led_39 (.in(_74164_4_pin12));
  LED led_40 (.in(_74164_5_pin5));
  LED led_41 (.in(_74164_5_pin6));
  LED led_42 (.in(_74164_4_pin13));
  LED led_43 (.in(_74164_6_pin3));
  LED led_44 (.in(_74164_5_pin3));
  LED led_45 (.in(_74164_5_pin4));
  _74164 _74164_5 (
    .pin1(_74164_5_pin1), .pin2(_74164_5_pin1), .pin3(_74164_5_pin3), .pin4(_74164_5_pin4),
    .pin5(_74164_5_pin5), .pin6(_74164_5_pin6), .pin7(1'b0), .pin8(clk), .pin9(button_1_out),
    .pin10(_74164_5_pin10), .pin11(_74164_5_pin11), .pin12(_74164_5_pin12), .pin13(_74164_3_pin1),
    .pin14(1'b1));
  _74164 _74164_6 (
    .pin1(_74164_4_pin13), .pin2(_74164_4_pin13), .pin3(_74164_6_pin3), .pin4(_74164_6_pin4),
    .pin5(_74164_6_pin5), .pin6(_74164_6_pin6), .pin7(1'b0), .pin8(clk), .pin9(button_1_out),
    .pin10(_74164_6_pin10), .pin11(_74164_6_pin11), .pin12(_74164_6_pin12), .pin13(_74164_6_pin13),
    .pin14(1'b1));
  LED led_46 (.in(_74164_6_pin4));
  LED led_47 (.in(_74164_6_pin5));
  LED led_48 (.in(_74164_7_pin12));
  LED led_49 (.in(_74164_5_pin1));
  LED led_50 (.in(_74164_6_pin6));
  LED led_51 (.in(_74164_6_pin10));
  LED led_52 (.in(_74164_7_pin10));
  LED led_53 (.in(_74164_7_pin11));
  LED led_54 (.in(_74164_6_pin11));
  LED led_55 (.in(_74164_6_pin12));
  LED led_56 (.in(_74164_7_pin5));
  LED led_57 (.in(_74164_7_pin6));
  LED led_58 (.in(_74164_6_pin13));
  LED led_59 (.in(_74164_7_pin3));
  LED led_60 (.in(_74164_7_pin4));
  _74164 _74164_7 (
    .pin1(_74164_7_pin1), .pin2(_74164_7_pin1), .pin3(_74164_7_pin3), .pin4(_74164_7_pin4),
    .pin5(_74164_7_pin5), .pin6(_74164_7_pin6), .pin7(1'b0), .pin8(clk), .pin9(button_1_out),
    .pin10(_74164_7_pin10), .pin11(_74164_7_pin11), .pin12(_74164_7_pin12), .pin13(_74164_5_pin1),
    .pin14(1'b1));
  LED led_61 (.in(_74164_8_pin3));
  LED led_62 (.in(_74164_8_pin4));
  LED led_63 (.in(_74164_8_pin5));
  LED led_64 (.in(_74164_8_pin6));
  LED led_65 (.in(_74164_8_pin10));
  LED led_66 (.in(_74164_8_pin11));
  LED led_67 (.in(_74164_8_pin12));
  LED led_68 (.in(_74164_8_pin13));
  LED led_69 (.in(_74164_9_pin3));
  LED led_70 (.in(_74164_9_pin4));
  LED led_71 (.in(_74164_9_pin5));
  LED led_72 (.in(_74164_9_pin6));
  LED led_73 (.in(_74164_9_pin10));
  LED led_74 (.in(_74164_9_pin11));
  LED led_75 (.in(_74164_9_pin12));
  LED led_76 (.in(_74164_7_pin1));
  _74164 _74164_8 (
    .pin1(_74164_6_pin13), .pin2(_74164_6_pin13), .pin3(_74164_8_pin3), .pin4(_74164_8_pin4),
    .pin5(_74164_8_pin5), .pin6(_74164_8_pin6), .pin7(1'b0), .pin8(clk), .pin9(button_1_out),
    .pin10(_74164_8_pin10), .pin11(_74164_8_pin11), .pin12(_74164_8_pin12), .pin13(_74164_8_pin13),
    .pin14(1'b1));
  _74164 _74164_9 (
    .pin1(_74164_8_pin13), .pin2(_74164_8_pin13), .pin3(_74164_9_pin3), .pin4(_74164_9_pin4),
    .pin5(_74164_9_pin5), .pin6(_74164_9_pin6), .pin7(1'b0), .pin8(clk), .pin9(button_1_out),
    .pin10(_74164_9_pin10), .pin11(_74164_9_pin11), .pin12(_74164_9_pin12), .pin13(_74164_7_pin1),
    .pin14(1'b1));

  // Notes on the sheet:
  //   clk: Hz: 50
  //   DATA
  //   DEMONSTRATOR
  //   DELAY-LINE MEMORY
  //   P-LAB
  //   CYCLE
  //   R/W
  //   DATA
  //   WRITE
  //   ADDRESS
  //   COUNTER
  //   QUEUED
  //   DATA
  //   RECIRCULATE
  //   WRITING
  //   CLEAR
  //   ALL
endmodule
